# Fritzing sketch colorsenser (saved by Fritzing 0.9.3b)
breadboards: 1

parts:
  パーツ1 = Arduino Uno (Rev3)
  e-radionica1 = TCS230 Color Sensor [part_number=101209]

nets:
  N1: パーツ1.D8, e-radionica1.Out
  N2: パーツ1.D12/MISO, e-radionica1.Vcc
  N3: パーツ1.D4, e-radionica1.S0
  N4: パーツ1.D5_PWM, e-radionica1.S1
  N5: パーツ1.D6_PWM, e-radionica1.S2
  N6: パーツ1.D7, e-radionica1.S3
  GND: パーツ1.GND, e-radionica1.Gnd, e-radionica1.OE

custom parts:
  TCS230 Color Sensor: TCS230
